# Fritzing sketch navsys_daughter_board (saved by Fritzing 0.9.3b)
stripboards: 1

parts:
  LED_Strip = Screw terminal - 2 pins [package=THT]
  5V_DC = Screw terminal - 2 pins [package=THT]
  part = Screw terminal - 2 pins [package=THT]
  IC1 = Logic Level Converter
  Pin_Header = Header 8 [package=1x08_smd]
  C1_2200_uF = Capacitor Polarized [package=cpol-radial-1000uf-25v]

nets:
  N1: LED_Strip.pin1, IC1.TX_HV
  N2: LED_Strip.pin2, 5V_DC.pin1, IC1.HV, Pin_Header.1, C1_2200_uF.+
  N3: 5V_DC.pin2, part.pin1, IC1.GND, Pin_Header.5, Pin_Header.8, C1_2200_uF.-
  N4: part.pin2, IC1.TX2_HV
  N5: IC1.TX2_LV, Pin_Header.7
  N6: IC1.LV, Pin_Header.4
  N7: IC1.TX_LV, Pin_Header.2
